// Digital circuit TrabalhoProjetos.dig as structural Verilog
module TrabalhoProjetos (
);

  wire multiplexer_1_out, multiplexer_2_out, registerbank_1_p1, registerbank_1_p4;
  wire [4:0] register_1_q;
  wire [31:0] ram32bit_1_p2, registerbank_1_p3, registerbank_1_p5, registerbank_1_p6, rom_1_d;

  Multiplexer multiplexer_1 (.in_0(registerbank_1_p1), .out(multiplexer_1_out));  // open: sel, in_1
  Register register_1 (.D(multiplexer_1_out), .Q(register_1_q[0]));  // open: C, en
  ROM #(.AddrBits(5), .Bits(32)) rom_1 (.A(register_1_q), .D(rom_1_d));  // open: sel
  Add add_1 (.a(rom_1_d[0]), .b(1'b0));  // open: c_i, s, c_o
  UnidadeDeControle unidadedecontrole_1 ();  // open: Opcode, memoryWrite, Branch, memoryRead, registerWrite, load_en, ALU_OP, A, B, NExt_PC, extender
  // RegisterBank registerbank_1: pin names not known; wires that end beside it: registerbank_1_p1, rom_1_d, registerbank_1_p3, registerbank_1_p4, registerbank_1_p5, registerbank_1_p6
  Multiplexer multiplexer_2 (.in_0(registerbank_1_p5[0]), .out(multiplexer_2_out));  // open: sel, in_1
  // ULA ula_1: pin names not known; wires that end beside it: registerbank_1_p4, multiplexer_2_out
  // RAM32Bit #(.generic("addrBits := ;")) ram32bit_1: pin names not known; wires that end beside it: registerbank_1_p5, ram32bit_1_p2
  Multiplexer #(.Bits(32), .Selector_Bits(2)) multiplexer_3 (
    .in_0(registerbank_1_p5), .in_1(ram32bit_1_p2), .in_2(registerbank_1_p6), .out(registerbank_1_p3));  // open: sel, in_3
  // Pins of 1 and 5 bits meet at register_1_q
  // Pins of 1 and 32 bits meet at rom_1_d
  // Pins of 1 and 32 bits meet at 32'h4
  // Pins of 1 and 32 bits meet at registerbank_1_p5

  // Notes on the sheet:
  //   unidade
  //   de controle
  //   extensor
  //   de
  //   imediato
endmodule
